# Fritzing sketch ard_BME280 (saved by Fritzing 0.9.3b)

parts:
  Εξάρτημα1 = Adafruit BMP280 [part_number="Adafruit #2651"]
  Εξάρτημα2 = Arduino Uno (Rev3)

nets:
  GND: Εξάρτημα1.GND, Εξάρτημα2.GND
  N1: Εξάρτημα1.SCK/SCL, Εξάρτημα2.A5/SCL
  N2: Εξάρτημα1.SDI/SDA, Εξάρτημα2.A4/SDA
  VCC: Εξάρτημα1.VCC, Εξάρτημα2.5V
  N3: Εξάρτημα1.SDO/ADR, Εξάρτημα2.D7

custom parts:
  Adafruit BMP280: Bosch has stepped up their game with their new BMP280 sensor, an environmental sensor with temperature, barometric pressure that is the next generation upgrade to the BMP085/BMP180/BMP183. This sensor is great for all sorts of weather sensing and can even be used in both I2C and SPI! This precision sensor from Bosch is the best low-cost, precision sensing solution for measuring barometric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
